# Fritzing sketch Wiring-perfboard (saved by Fritzing 0.9.3b)
perfboards: 1

parts:
  SparkFun_Pro_Micro1 = SparkFun Pro Micro [part_number=DEV-12640]
  J1 = male pin header, 12 pins [form="♂ (male)"]
  J2 = male pin header, 12 pins [form="♂ (male)"]  # not connected
  J3 = male pin header, 5 pins [form="♂ (male)"]
  J4 = male pin header, 5 pins [form="♂ (male)"]
  J5 = male pin header, 5 pins [form="♂ (male)"]
  X1 = DB9 Connector [package=db9]
  X2 = DB9 Connector [package=db9]

nets:
  N1: SparkFun_Pro_Micro1.GND, J4.pin3, J5.pin5, X1.1, X2.6
  N2: SparkFun_Pro_Micro1.VCC, J3.pin4, J3.pin5, X2.7, X2.9
  N3: SparkFun_Pro_Micro1.A2, J5.pin2, X1.4
  N4: SparkFun_Pro_Micro1.A1, J5.pin3, X1.3
  N5: SparkFun_Pro_Micro1.A0, J5.pin4, X1.2
  N6: SparkFun_Pro_Micro1.D9, J4.pin4, X2.8
  N7: SparkFun_Pro_Micro1.D8, J4.pin2, X2.4
  N8: SparkFun_Pro_Micro1.D4, J3.pin2, X2.3
  N9: SparkFun_Pro_Micro1.RXI, J4.pin1, X2.2
  N10: SparkFun_Pro_Micro1.TXO, J1.pin1, J3.pin1, X2.1
  N11: J5.pin1, X1.9

custom parts:
  SparkFun Pro Micro: This tiny little board does all of the neat-o Arduino tricks that you’re familiar with: 4 channels of 10-bit ADC, 5 PWM pins, 12 DIOs as well as hardware serial connections Rx and Tx. Running at 16MHz and 5V, this board will remind you a lot of your other favorite Arduino-compatible boards but this little guy can go just about anywhere. There is a voltage regulator on board so it can accept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
